# Fritzing sketch schematic v02 (saved by Fritzing 1.0.1rc)
breadboards: 1

parts:
  Pololu_A1 = Pololu A4988 [package=SO16]
  C1 = Electrolytic Capacitor [capacitance=100µF voltage=35V package="200 mil [THT, electrolytic]"]
  Raspberry_Pi1 = Raspberry Pi Zero

nets:
  N1: Pololu_A1.RESET, Pololu_A1.SLEEP
  N2: Pololu_A1.STEP, Raspberry_Pi1.GIPO20
  N3: Pololu_A1.DIR, Raspberry_Pi1.GIPO21
  N4: Pololu_A1.GND#8, Raspberry_Pi1.GND
  VDD: Pololu_A1.VDD, Raspberry_Pi1.5V
  N5: Pololu_A1.GND#14, C1.+
  N6: Pololu_A1.VMOT, C1.-

custom parts:
  Raspberry Pi Zero: The Raspberry Pi Zero is the latest single board computer to be released by the Raspberry Pi Foundation. It is the entry level model Raspberry Pi perfect for hobbyists, makers and industrial engineers looking to create solutions where small size and low power consumption are important. This is especially relevant for applications in the wearables space as well as up and coming applications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
